# Fritzing sketch Water_Me (saved by Fritzing 0.9.3b)
breadboards: 1

parts:
  Bauteil1 = Soil Moisture Sensor
  Bauteil2 = Arduino Nano (Rev3.0)
  LED1 = RGB LED (com. cathode, rgb) [package="5 mm [THT]"]
  R1 = Resistor [tolerance=±5% resistance=100 package=THT]

nets:
  N1: Bauteil1.SIG, Bauteil2.A1
  GND: Bauteil1.GND, Bauteil2.GND, R1.Pin_1
  VCC: Bauteil1.VCC, Bauteil2.5V
  N2: Bauteil2.D2, LED1.red_anode
  N3: Bauteil2.D3, LED1.common_cathode
  N4: Bauteil2.D4, LED1.blue_anode
  N5: LED1.green_anode, R1.Pin_0
